// Digital circuit CPU_ARQCOMP.dig as structural Verilog
module CPU_ARQCOMP (
  input  clk
);

  wire FRZ, RST, u_Hazard_Detection_stall_hazard, u_MemLoader_mem_loading;
  wire [7:0] u_MemLoader_loader_addr;
  wire [23:8] u_MemLoader_loader_addr_2;
  wire [31:0] multiplexer_1_out, register_2_q, rom_2_d;
  wire [31:2] undriven;

  Control_Unit #(.applicationType("GHDL"), .CodeFile("C:\\TECH\\RISC-V\\Control_Unit_v2.vhd")) u_Control_Unit ();  // open: opcode, funct3, raw_vew, AluSrc, blockA, RegWrite, MemRead, MemWrite, Branch, BranchNotEq, BrIncond, regToPC, AluOp, regSrc, vec_enable, vec_mode
  Register #(.Bits(32)) register_1 ();  // open: D, C, en, Q
  EXMEM #(.applicationType("GHDL"), .CodeFile("C:\\TECH\\RISC-V\\EXMEM_v2.vhd")) u_EXMEM ();  // open: clk, freeze, sumIn, zeroIn, aluIn, read2In, wbAddIn, WBin, Min, pcPl4In, pcOut, zeroOut, aluOut, read2Out, wbAddOut, WBout, Mout, pcPl4Out
  ALU #(.applicationType("GHDL"), .CodeFile("C:\\TECH\\RISC-V\\ALU_v2.vhd")) u_ALU ();  // open: A, B, control, vec_mode, result, zero
  Multiplexer #(.Bits(32)) multiplexer_1 (.sel(RST), .in_1({32{1'b0}}), .out(multiplexer_1_out));  // open: in_0
  RAMDualPort #(.Bits(32)) ramdualport_1 (.A(undriven[3:2]));  // open: Din, str, C, ld, D
  Register #(.Bits(32)) register_2 (.D(multiplexer_1_out), .C(clk), .Q(register_2_q));  // open: en
  MEMWB #(.applicationType("GHDL"), .CodeFile("C:\\TECH\\RISC-V\\MEMWB_v2.vhd")) u_MEMWB ();  // open: clk, freeze, readIn, aluIn, wbAddIn, WBin, pcPl4In, pcPlIIn, readOut, aluOut, wbAddOut, WBout, pcPl4Out, pcPlIOut
  ROM #(.Bits(32)) rom_1 (.A(register_2_q[1:0]), .sel(1'b1));  // open: D
  IDEX #(.applicationType("GHDL"), .CodeFile("C:\\TECH\\RISC-V\\IDEX_v2.vhd")) u_IDEX (
    .clk(clk), .freeze(FRZ));  // open: pcIn, read1In, read2In, immGenIn, aluControlin, wbAddIn, WBin, Min, EXin, pcPl4In, rs1In, rs2In, pcOut, read1Out, read2Out, immGenOut, aluControlout, wbAddOut, WBout, Mout, EXout, pcPl4Out, rs1Out, rs2Out
  Hazard_Detection #(.applicationType("GHDL"), .CodeFile("C:\\TECH\\RISC-V\\Hazard_Unit.vhd")) u_Hazard_Detection (.stall_hazard(u_Hazard_Detection_stall_hazard));  // open: IDEX_MemRead, IDEX_RegisterRd, IFID_RegisterRs1, IFID_RegisterRs2
  Button button_1 (.out(RST));
  ROM #(.AddrBits(8), .Bits(32)) rom_2 (.A(u_MemLoader_loader_addr), .sel(1'b1), .D(rom_2_d));
  MemLoader #(.applicationType("GHDL"), .CodeFile("C:\\TECH\\RISC-V\\MemLoader_v2.vhd")) u_MemLoader (
    .clk(clk), .reset(RST), .src_data(rom_2_d),
    .loader_addr({u_MemLoader_loader_addr_2, u_MemLoader_loader_addr}), .mem_loading(u_MemLoader_mem_loading));  // open: loader_data, loader_we
  Freeze_Control #(.applicationType("GHDL"), .CodeFile("C:\\TECH\\RISC-V\\Freeze_Control.vhd")) u_Freeze_Control (
    .stall_hazard(u_Hazard_Detection_stall_hazard), .mem_loading(u_MemLoader_mem_loading), .deep_freeze(FRZ));  // open: pc_ifid_freeze
  // Pins of 2 and 30 bits meet at undriven
  // Pins of 2 and 32 bits meet at register_2_q
endmodule
