// Digital circuit CPU_ARQCOMP_final.dig as structural Verilog
module CPU_ARQCOMP_final (
  input  [31:0] clk
);

  wire FRZ, IMM, PCSrc, RST, u_ALU_zero, u_Hazard_Detection_stall_hazard, u_MemLoader_mem_loading,
       u_PCSrc_Control_take_cond, u_PCSrc_Control_take_uncond, undriven, undriven_2, undriven_3;
  wire [1:0] u_MEMWB_wbout;
  wire [2:0] u_Control_Unit_regwrite, u_EXMEM_wbout, u_IDEX_wbout;
  wire [3:0] u_ALU_Control_control, u_Control_Unit_alusrc, u_IDEX_exout;
  wire [4:0] u_EXMEM_wbaddout, u_IDEX_wbaddout;
  wire [5:0] u_EXMEM_mout, u_IDEX_mout;
  wire [7:0] u_MemLoader_loader_addr;
  wire [23:8] u_MemLoader_loader_addr_2;
  wire [29:0] undriven_6;
  wire [31:0] multiplexer_1_out, multiplexer_2_out, multiplexer_3_out, register_2_q, rom_1_d, rom_2_d,
       u_ALU_result, u_EXMEM_aluout, u_EXMEM_pcpl4out, u_IDEX_immgenout, u_IDEX_pcpl4out, u_IDEX_read1out,
       u_IDEX_read2out, u_ImmGen_imm, u_PC2_pc_out, u_register_file_outa, u_somador_z;
  wire [31:1] undriven_4, undriven_5;
  wire [31:7] u_IFID_instout;

  Button button_1 (.out(RST));
  Hazard_Detection #(.applicationType("GHDL"), .CodeFile("C:\\TECH\\RISC-V\\Hazard_Unit.vhd")) u_Hazard_Detection (.stall_hazard(u_Hazard_Detection_stall_hazard));  // open: IDEX_MemRead, IDEX_RegisterRd, IFID_RegisterRs1, IFID_RegisterRs2
  ROM #(.AddrBits(8), .Bits(32)) rom_1 (.A(u_MemLoader_loader_addr), .sel(1'b1), .D(rom_1_d));
  PC2 #(.applicationType("GHDL")) u_PC2 (
    .clk(clk[3]), .reset(RST), .pc_in(multiplexer_1_out), .writeEnableL(undriven), .pc_out(u_PC2_pc_out));
  Freeze_Control #(.applicationType("GHDL"), .CodeFile("C:\\TECH\\RISC-V\\Freeze_Control.vhd")) u_Freeze_Control (
    .stall_hazard(u_Hazard_Detection_stall_hazard), .mem_loading(u_MemLoader_mem_loading), .deep_freeze(FRZ));  // open: pc_ifid_freeze
  MemLoader #(.applicationType("GHDL"), .CodeFile("C:\\TECH\\RISC-V\\MemLoader_v2.vhd")) u_MemLoader (
    .clk(clk[3]), .reset(RST), .src_data(rom_1_d),
    .loader_addr({u_MemLoader_loader_addr_2, u_MemLoader_loader_addr}), .mem_loading(u_MemLoader_mem_loading));  // open: loader_data, loader_we
  somador #(.applicationType("GHDL")) u_somador (.A(u_PC2_pc_out), .B(32'h4), .Z(u_somador_z));
  ROM #(.AddrBits(8), .Bits(32)) rom_2 (.A(u_PC2_pc_out[7:0]), .sel(1'b1), .D(rom_2_d));
  IFID #(.applicationType("GHDL")) u_IFID (
    .clk(clk[3]), .pcIn(u_PC2_pc_out), .writeEnableL(undriven), .instIn(rom_2_d),
    .instOut({u_IFID_instout[31], clk[3], u_IFID_instout[29:25], clk[4:3], {3{clk[3]}}, clk[4:3], {6{clk[3]}}, u_IFID_instout[11:7], clk[6:3], {3{clk[3]}}}));  // open: pcPl4In, pcOut, pcPl4Out
  Multiplexer multiplexer_1 (.sel(PCSrc), .in_0(u_somador_z[0]), .in_1(IMM), .out(multiplexer_1_out[0]));
  ImmGen #(.applicationType("GHDL")) u_ImmGen (
    .inst({u_IFID_instout[31], clk[3], u_IFID_instout[29:25], clk[4:3], {3{clk[3]}}, clk[4:3], {6{clk[3]}}, u_IFID_instout[11:7], clk[6:3], {3{clk[3]}}}),
    .imm(u_ImmGen_imm));
  IDEX #(.applicationType("GHDL"), .CodeFile("C:\\TECH\\RISC-V\\IDEX_v2.vhd")) u_IDEX (
    .clk(clk[3]), .freeze(FRZ), .read1In(u_register_file_outa), .read2In({clk[31:3], {3{clk[3]}}}),
    .immGenIn(u_ImmGen_imm), .aluControlin({4{clk[3]}}), .wbAddIn(u_IFID_instout[11:7]),
    .WBin(u_Control_Unit_regwrite), .Min({clk[5:3], {3{clk[3]}}}), .EXin(u_Control_Unit_alusrc),
    .read1Out(u_IDEX_read1out), .read2Out(u_IDEX_read2out), .immGenOut(u_IDEX_immgenout),
    .wbAddOut(u_IDEX_wbaddout), .WBout(u_IDEX_wbout), .Mout(u_IDEX_mout), .EXout(u_IDEX_exout),
    .pcPl4Out(u_IDEX_pcpl4out));  // open: pcIn, pcPl4In, rs1In, rs2In, pcOut, aluControlout, rs1Out, rs2Out
  register_file #(.applicationType("GHDL")) u_register_file (
    .\input ({clk[31:3], {3{clk[3]}}}), .writeEnable(clk[3]), .regASel({clk[4:3], {3{clk[3]}}}),
    .regBSel({clk[4:3], {3{clk[3]}}}), .writeRegSel({clk[4:3], {3{clk[3]}}}), .clk(clk[3]),
    .outA(u_register_file_outa), .outB({clk[31:3], {3{clk[3]}}}));  // open: regSelManual, outRegManual
  Control_Unit #(.applicationType("GHDL"), .CodeFile("C:\\TECH\\RISC-V\\Control_Unit_v2.vhd")) u_Control_Unit (
    .opcode({clk[6:3], {3{clk[3]}}}), .funct3({3{clk[3]}}), .raw_vew({2{clk[3]}}),
    .AluSrc(u_Control_Unit_alusrc[0]), .blockA(u_Control_Unit_alusrc[1]),
    .RegWrite(u_Control_Unit_regwrite[0]), .MemRead(clk[3]), .MemWrite(clk[3]), .Branch(clk[3]),
    .BranchNotEq(clk[3]), .BrIncond(clk[4]), .regToPC(clk[5]), .AluOp(u_Control_Unit_alusrc[3:2]),
    .regSrc(u_Control_Unit_regwrite[2:1]));  // open: vec_enable, vec_mode
  ALU_Control #(.applicationType("GHDL")) u_ALU_Control (
    .AluOp(u_IDEX_exout[1:0]), .Control(u_ALU_Control_control));  // open: Functs
  Multiplexer multiplexer_2 (
    .sel(u_IDEX_exout[2]), .in_0(u_IDEX_read2out[0]), .in_1(u_IDEX_immgenout[0]), .out(multiplexer_2_out[0]));
  Register #(.Bits(32)) register_1 ();  // open: D, C, en, Q
  ALU #(.applicationType("GHDL"), .CodeFile("C:\\TECH\\RISC-V\\ALU_v2.vhd")) u_ALU (
    .A(u_IDEX_read1out), .B(multiplexer_2_out), .control(u_ALU_Control_control), .vec_mode(2'b10),
    .result(u_ALU_result), .zero(u_ALU_zero));
  EXMEM #(.applicationType("GHDL"), .CodeFile("C:\\TECH\\RISC-V\\EXMEM_v2.vhd")) u_EXMEM (
    .clk(clk[3]), .freeze(FRZ), .zeroIn(1'b0), .aluIn(u_ALU_result), .read2In(u_IDEX_read2out),
    .wbAddIn(u_IDEX_wbaddout), .WBin(u_IDEX_wbout), .Min(u_IDEX_mout), .pcPl4In(u_IDEX_pcpl4out),
    .aluOut(u_EXMEM_aluout), .wbAddOut(u_EXMEM_wbaddout), .WBout(u_EXMEM_wbout), .Mout(u_EXMEM_mout),
    .pcPl4Out(u_EXMEM_pcpl4out));  // open: sumIn, pcOut, zeroOut, read2Out
  Multiplexer #(.Bits(32)) multiplexer_3 (.sel(RST), .in_1({32{1'b0}}), .out(multiplexer_3_out));  // open: in_0
  PCSrc_Control #(.applicationType("GHDL"), .CodeFile("C:\\TECH\\RISC-V-P1\\components\\PCSrc.vhd")) u_PCSrc_Control (
    .Branch(u_EXMEM_mout[0]), .BranchNotEq(undriven_3), .BrIncond(undriven_2), .zero(u_ALU_zero),
    .pcsrc(PCSrc), .take_cond(u_PCSrc_Control_take_cond), .take_uncond(u_PCSrc_Control_take_uncond));
  Register #(.Bits(32)) register_2 (.D(multiplexer_3_out), .C(clk[3]), .Q(register_2_q));  // open: en
  ROM #(.Bits(32)) rom_3 (.A(register_2_q[1:0]), .sel(1'b1));  // open: D
  Forward #(.applicationType("GHDL")) u_Forward (.clk(clk[3]));  // open: regWriteWB, regWriteMEM, RSrc1, RSrc2, RDWB, RDMEM, forwardA, forwardB
  LED led_1 (.in(u_PCSrc_Control_take_cond));
  LED led_2 (.in(u_PCSrc_Control_take_uncond));
  MEMWB #(.applicationType("GHDL"), .CodeFile("C:\\TECH\\RISC-V\\MEMWB_v2.vhd")) u_MEMWB (
    .clk(clk[3]), .freeze(FRZ), .readIn({undriven_4, 1'b0}), .aluIn(u_EXMEM_aluout),
    .wbAddIn(u_EXMEM_wbaddout), .WBin(u_EXMEM_wbout), .pcPl4In(u_EXMEM_pcpl4out),
    .pcPlIIn({undriven_5, 1'b0}), .aluOut({clk[31:3], {3{clk[3]}}}), .wbAddOut({clk[4:3], {3{clk[3]}}}),
    .WBout({clk[3], u_MEMWB_wbout}));  // open: readOut, pcPl4Out, pcPlIOut
  somador #(.applicationType("GHDL")) u_somador_2 ();  // open: A, B, Z
  RAMDualPort #(.Bits(32)) ramdualport_1 (.A(undriven_6[1:0]));  // open: Din, str, C, ld, D
  // Pins of 1 and 32 bits meet at multiplexer_2_out
  // Pins of 1 and 2 and 3 and 4 and 5 and 6 and 7 and 32 bits meet at {clk[31:3], {3{clk[3]}}}
  // Pins of 2 and 30 bits meet at undriven_6
  // Pins of 1 and 32 bits meet at u_IDEX_read2out
  // Pins of 1 and 6 bits meet at u_EXMEM_mout
  // Pins of 1 and 32 bits meet at u_IDEX_immgenout
  // Pins of 1 and 32 bits meet at {undriven_4, 1'b0}
  // Pins of 1 and 32 bits meet at {undriven_5, 1'b0}
  // Pins of 2 and 32 bits meet at register_2_q
  // Pins of 1 and 32 bits meet at multiplexer_1_out
  // Pins of 8 and 32 bits meet at u_PC2_pc_out
  // Pins of 1 and 32 bits meet at u_somador_z

  assign clk[2:0] = {3{clk[3]}};
endmodule

/* Code of PC2:
LIBRARY ieee;
USE ieee.std_logic_1164.all;

ENTITY PC2 IS
  PORT (
    clk      : IN  std_logic;
    reset    : IN  std_logic;
    pc_in    : IN  std_logic_vector(31 DOWNTO 0);
    writeEnableL   : IN std_logic;
    pc_out   : OUT std_logic_vector(31 DOWNTO 0)
    );
END PC2;

ARCHITECTURE TypeArchitecture OF PC2 IS
BEGIN
    PROCESS (clk, reset, writeEnableL)
    BEGIN
        IF (rising_edge(clk)) THEN
            if (pc_in = "UUUUUUUUUUUUUUUUUUUUUUUUUUUUUUUU") then
                pc_out <= (others => '0');
            elsif (writeEnableL = '0') then
                pc_out <= pc_in;
            end if;
        END IF;
        IF (reset = '1') THEN
            pc_out <= (others => '0');
        END IF;
    END PROCESS;
END TypeArchitecture;
*/

/* Code of somador:
LIBRARY ieee;
USE ieee.std_logic_1164.all;
USE IEEE.std_logic_unsigned.ALL;

ENTITY somador IS
  PORT (
    A, B : IN  std_logic_vector(31 DOWNTO 0);
    Z    : OUT std_logic_vector(31 DOWNTO 0)
    );
END somador;

ARCHITECTURE TypeArchitecture OF somador IS
BEGIN
Z <= A + B;
END TypeArchitecture;
*/

/* Code of IFID:
LIBRARY ieee;
USE ieee.std_logic_1164.all;

ENTITY IFID IS
  PORT (
    clk         : IN  std_logic;
    pcIn        : IN  std_logic_vector(31 DOWNTO 0);
    pcPl4In	 : IN  std_logic_vector(31 downto 0);
    writeEnableL   : IN std_logic;
    instIn      : IN  std_logic_vector(31 DOWNTO 0);
    pcOut       : OUT std_logic_vector(31 DOWNTO 0);
    pcPl4Out	 : OUT std_logic_vector(31 downto 0);
    instOut     : OUT std_logic_vector(31 DOWNTO 0)
    );
END IFID;

ARCHITECTURE TypeArchitecture OF IFID IS
SIGNAL IDIF : std_logic_vector(95 DOWNTO 0);
BEGIN
	PROCESS (clk, writeEnableL)
	BEGIN
		IF (rising_edge(clk)) THEN
			if (writeEnableL = '0') then
				IDIF(31 DOWNTO 0) <= instIn;
				IDIF(63 DOWNTO 32) <= pcIn;
				IDIF(95 downto 64) <= pcPl4In;
			end if;
		END IF;
		IF (falling_edge(clk)) THEN
			pcOut <= IDIF(63 DOWNTO 32);
			instOut <= IDIF(31 DOWNTO 0);
			pcPl4Out <= IDIF(95 downto 64);
		END IF;
	END PROCESS;
END TypeArchitecture;
*/

/* Code of ImmGen:
library IEEE;
use IEEE.STD_LOGIC_1164.ALL;
USE IEEE.NUMERIC_STD.ALL;

entity ImmGen is
    Port( 
        inst: in std_logic_vector(31 downto 0);  -- Entrada da instrução (32 bits)
        imm: out std_logic_vector(31 downto 0)   -- Saída do valor imediato gerado (32 bits)
        );
end ImmGen;

architecture Behavioral of ImmGen is
    signal opcode      : std_logic_vector(6 downto 0);
    signal imm_interno : std_logic_vector(31 downto 0);
begin

    opcode <= inst(6 downto 0);

    process(opcode, inst)
    begin
        -- Default zera tudo antes de cada caso, evita inferir latch
        imm_interno <= (others => '0');

        case opcode is
            -- I-type: addi/andi/ori/slti/etc (0010011), load (0000011), jalr (1100111)
            when "0010011" | "0000011" | "1100111" =>
                imm_interno(11 downto 0)  <= inst(31 downto 20);
                imm_interno(31 downto 12) <= (others => inst(31));

            -- U-type: lui (0110111), auipc (0010111)
            when "0110111" | "0010111" =>
                imm_interno(31 downto 12) <= inst(31 downto 12);
                imm_interno(11 downto 0)  <= (others => '0');

            -- S-type: sw (0100011)
            when "0100011" =>
                imm_interno(11 downto 5)  <= inst(31 downto 25);
                imm_interno(4 downto 0)   <= inst(11 downto 7);
                imm_interno(31 downto 12) <= (others => inst(31));

            -- SB-type: beq/bne (1100011)
            when "1100011" =>
                imm_interno(12)           <= inst(31);
                imm_interno(11)           <= inst(7);
                imm_interno(10 downto 5)  <= inst(30 downto 25);
                imm_interno(4 downto 1)   <= inst(11 downto 8);
                imm_interno(0)            <= '0';
                imm_interno(31 downto 13) <= (others => inst(31));

            -- UJ-type: jal (1101111)
            when "1101111" =>
                imm_interno(20)           <= inst(31);
                imm_interno(19 downto 12) <= inst(19 downto 12);
                imm_interno(11)           <= inst(20);
                imm_interno(10 downto 1)  <= inst(30 downto 21);
                imm_interno(0)            <= '0';
                imm_interno(31 downto 21) <= (others => inst(31));

            when others =>
                imm_interno <= (others => '0');
        end case;
    end process;

    imm <= imm_interno;

end Behavioral;
*/

/* Code of register_file:
library ieee;
use ieee.std_logic_1164.all;
use ieee.numeric_std.all;

entity register_file is
  port(
    outA        : out std_logic_vector(31 downto 0);
    outB        : out std_logic_vector(31 downto 0);
    input       : in  std_logic_vector(31 downto 0);
    regSelManual: in  std_logic_vector(4 downto 0);
    outRegManual: out std_logic_vector(31 downto 0);
    writeEnable : in  std_logic;
    regASel     : in  std_logic_vector(4 downto 0);
    regBSel     : in  std_logic_vector(4 downto 0);
    writeRegSel : in  std_logic_vector(4 downto 0);
    clk         : in  std_logic
    );
end register_file;

architecture TypeArchitecture of register_file is
  type registerFile is array(0 to 31) of std_logic_vector(31 downto 0);
  signal registers : registerFile :=
   ("00000000000000000000000000010000","00000000000000000000000000000001","00000000000000000000000000000000","00000000000000000000000000000000",
    "00000000000000000000000000000000","00000000000000000000000000000000","00000000000000000000000000000000","00000000000000000000000000000000",
    "00000000000000000000000000000000","00000000000000000000000000000000","00000000000000000000000000000000","00000000000000000000000000000000",
    "00000000000000000000000000000000","00000000000000000000000000000000","00000000000000000000000000000000","00000000000000000000000000000000",
    "00000000000000000000000000000000","00000000000000000000000000000000","00000000000000000000000000000000","00000000000000000000000000000000",
    "00000000000000000000000000000000","00000000000000000000000000000000","00000000000000000000000000000000","00000000000000000000000000000000",
    "00000000000000000000000000000000","00000000000000000000000000000000","00000000000000000000000000000000","00000000000000000000000000000000",
    "00000000000000000000000000000000","00000000000000000000000000000000","00000000000000000000000000000000","00000000000000000000000000000000");

begin
  regFile : process (clk) is
  begin
    if rising_edge(clk) then
      if (registers(to_integer(unsigned(regASel))) = "UUUUUUUUUUUUUUUUUUUUUUUUUUUUUUUU") THEN
        outA <= (others => '0');
      ELSE
        outA <= registers(to_integer(unsigned(regASel)));
      END IF;
      IF (registers(to_integer(unsigned(regBSel))) = "UUUUUUUUUUUUUUUUUUUUUUUUUUUUUUUU") THEN
        outB <= (others => '0');
      ELSE
        outB <= registers(to_integer(unsigned(regBSel)));
      END IF;
      if writeEnable = '1' then
        registers(to_integer(unsigned(writeRegSel))) <= input;
        if regASel = writeRegSel then
          outA <= input;
        end if;
        if regBSel = writeRegSel then
          outB <= input;
        end if;
      end if;
    end if;
  end process;

  outRegManual <= registers(to_integer(unsigned(regSelManual)));

end TypeArchitecture;
*/

/* Code of ALU_Control:
library IEEE;
use IEEE.STD_LOGIC_1164.ALL;

entity ALU_Control is
    port(
        Functs    : IN std_logic_vector(3 downto 0);
        AluOp   : IN std_logic_vector(1 downto 0);
        Control : OUT std_logic_vector(3 downto 0)
        );
end ALU_Control;

architecture TypeArchitecture of ALU_Control is
begin
    control <= "0010" when AluOp = "00" else
             "0110" when AluOp = "01" else
             "0010" when Functs = "0000" else
             "0110" when Functs = "1000" else
             "0011" when Functs = "0001" else
             "0101" when Functs = "0100" else
             "0111" when Functs = "0101" else
             "0001" when Functs = "0110" else
             "0000" when Functs = "0111";

end TypeArchitecture;
*/

/* Code of Forward:
library IEEE;
use IEEE.STD_LOGIC_1164.ALL;

entity Forward is
	port(
	     clk					: IN std_logic;
	     regWriteWB, regWriteMEM 	: IN std_logic;
	     RSrc1, RSrc2			: IN std_logic_vector(4 downto 0);
	     RDWB, RDMEM			: IN std_logic_vector(4 downto 0);
	     forwardA, forwardB		: OUT std_logic_vector(1 downto 0)
     );
end Forward;

architecture TypeArchitecture of Forward is
	signal forwardA_interno, forwardB_interno : std_logic_vector(1 downto 0) := "00";

begin
	process(clk)
    begin
        if ((regWriteMEM = '1') and (not(RDMEM = "00000")) and (RDMEM = RSrc1)) then
        	forwardA_interno <= "10";
        end if;

        if ((regWriteMEM = '1') and (not(RDMEM = "00000")) and (RDMEM = RSrc2)) then
        	forwardB_interno <= "10";
        end if;

        if ((regWriteWB = '1') and (not(RDWB = "00000")) and (RDWB = RSrc1)) then
        	forwardA_interno <= "01";
        end if;

        if ((regWriteWB = '1') and (not(RDWB = "00000")) and (RDWB = RSrc2)) then
        	forwardB_interno <= "01";
        end if;

    end process;

    forwardA <= forwardA_interno;
    forwardB <= forwardB_interno;
end TypeArchitecture;
*/
